// Logisim project watermelon_one.circ as structural Verilog: 9 circuits, main circuit main
module main (
  input  [31:0] in_1,
  input  in_2,
  input  in_3,
  input  in_4
);

  wire [2:0] rom_1_p4;
  wire [4:0] rom_1_p3, rom_1_p4_2, rom_1_p5_2;
  wire [6:0] rom_1_p5;
  wire [7:1] rom_1_p2;
  wire [31:0] program_counter_1_o;

  program_counter program_counter_1 (
    .Y(in_1), .OE(in_2), .C(in_3), .CL(in_4), .O(program_counter_1_o));  // open: D, SWIN
  // Probe on program_counter_1_o
  // ROM #(.addrWidth(19), .line("quad")) rom_1: pin names not known; wires that end beside it: program_counter_1_o[18:0], {rom_1_p2, rom_1_p3[4]}, {rom_1_p3[3:0], rom_1_p4_2[4:1]}, {rom_1_p4_2[0], rom_1_p4, rom_1_p5_2[4:1]}, {rom_1_p5_2[0], rom_1_p5}
  // Probe on {rom_1_p2, rom_1_p3, rom_1_p4_2, rom_1_p4, rom_1_p5_2, rom_1_p5}
  register_file register_file_1 (
    .R1A(rom_1_p4_2), .R2A(rom_1_p3), .WRITE_ADDR(rom_1_p5_2));  // open: WRITE, LOAD, CLOCK, WRITE_DATA, CLR_x0, R1O, R2O

  // Notes on the sheet:
  //   contents of rom_1 (hex, n*v repeats v):
  //   7*0 11 0 0 0 22 0 0 0 33 0 0 0 44 0 0 0 55 0 0 0 66 0 0 0 77 0 0 0 88 0 0 0 99 0 0 11 11 0 0 22 22
endmodule

module octal_D_flip_flop (
  input  OE,
  input  C,
  input  CL,
  input  [7:0] D,
  output [7:0] O
);

  wire [7:0] d_ff_1_q;

  D_Flip_Flop d_ff_1 (.D(D[0]), .clk(C), .Q(d_ff_1_q[0]), .reset(CL));  // open: Qn, preset
  D_Flip_Flop d_ff_2 (.D(D[1]), .clk(C), .Q(d_ff_1_q[1]), .reset(CL));  // open: Qn, preset
  D_Flip_Flop d_ff_3 (.D(D[2]), .clk(C), .Q(d_ff_1_q[2]), .reset(CL));  // open: Qn, preset
  D_Flip_Flop d_ff_4 (.D(D[3]), .clk(C), .Q(d_ff_1_q[3]), .reset(CL));  // open: Qn, preset
  D_Flip_Flop d_ff_5 (.D(D[4]), .clk(C), .Q(d_ff_1_q[4]), .reset(CL));  // open: Qn, preset
  D_Flip_Flop d_ff_6 (.D(D[5]), .clk(C), .Q(d_ff_1_q[5]), .reset(CL));  // open: Qn, preset
  D_Flip_Flop d_ff_7 (.D(D[6]), .clk(C), .Q(d_ff_1_q[6]), .reset(CL));  // open: Qn, preset
  D_Flip_Flop d_ff_8 (.D(D[7]), .clk(C), .Q(d_ff_1_q[7]), .reset(CL));  // open: Qn, preset
  assign O = OE ? d_ff_1_q : 8'bz;  // Controlled_Buffer controlled_buffer_1
endmodule

module register_8_bit (
  input  OE,
  input  WE,
  input  C,
  input  CL,
  input  [7:0] D,
  output [7:0] O
);

  wire and_1_out;

  and and_1 (and_1_out, WE, C);
  octal_D_flip_flop octal_d_flip_flop_1 (.OE(OE), .C(and_1_out), .CL(CL), .D(D), .O(O));
endmodule

module program_counter (
  input  [31:0] Y,
  input  [31:0] D,
  input  SWIN,
  input  OE,
  input  C,
  input  CL,
  output [31:0] O
);

  wire [7:0] multiplexer_1_out, multiplexer_2_out, multiplexer_3_out, multiplexer_4_out;
  wire [31:0] adder_1_out;

  Multiplexer #(.width(8)) multiplexer_1 (.in0(adder_1_out[7:0]), .in1(D[7:0]), .out(multiplexer_1_out), .sel(SWIN));
  Adder #(.width(32)) adder_1 (.a(Y), .b(O), .out(adder_1_out));  // open: cin, cout
  Multiplexer #(.width(8)) multiplexer_2 (.in0(adder_1_out[15:8]), .in1(D[15:8]), .out(multiplexer_2_out), .sel(SWIN));
  Multiplexer #(.width(8)) multiplexer_3 (
    .in0(adder_1_out[23:16]), .in1(D[23:16]), .out(multiplexer_3_out), .sel(SWIN));
  Multiplexer #(.width(8)) multiplexer_4 (
    .in0(adder_1_out[31:24]), .in1(D[31:24]), .out(multiplexer_4_out), .sel(SWIN));
  octal_D_flip_flop octal_d_flip_flop_1 (.OE(OE), .C(C), .CL(CL), .D(multiplexer_1_out), .O(O[7:0]));
  octal_D_flip_flop octal_d_flip_flop_2 (.OE(OE), .C(C), .CL(CL), .D(multiplexer_2_out), .O(O[15:8]));
  octal_D_flip_flop octal_d_flip_flop_3 (.OE(OE), .C(C), .CL(CL), .D(multiplexer_3_out), .O(O[23:16]));
  octal_D_flip_flop octal_d_flip_flop_4 (.OE(OE), .C(C), .CL(CL), .D(multiplexer_4_out), .O(O[31:24]));

  // Notes on the sheet:
  //   Y: initial=0x4
endmodule

module register_file (
  input  [4:0] R1A,
  input  [4:0] R2A,
  input  WRITE,
  input  LOAD,
  input  CLOCK,
  input  [4:0] WRITE_ADDR,
  input  [31:0] WRITE_DATA,
  input  CLR_x0,
  output [31:0] R1O,
  output [31:0] R2O
);

  wire and_2_out, and_3_out, and_4_out, multiplexer_4_out, not_1_out, not_2_out, not_3_out, not_4_out,
       not_5_out, not_6_out, not_7_out, not_8_out, not_9_out, not_10_out, not_11_out, not_12_out, not_13_out,
       not_14_out, not_15_out, not_16_out, not_17_out, not_18_out, not_19_out, not_20_out, not_21_out,
       not_22_out, not_23_out, not_24_out, not_25_out, not_26_out, not_27_out, not_28_out, not_29_out,
       not_30_out, not_31_out, not_32_out, not_33_out, not_34_out, not_35_out, not_36_out, not_37_out,
       not_38_out, not_39_out, not_40_out, or_1_out, or_2_out, or_3_out;
  wire [0:0] and_1_out, multiplexer_1_out;
  wire [4:0] multiplexer_2_out, multiplexer_3_out;
  wire [31:0] controlled_buffer_1_out, multiplexer_5_out;

  or or_1 (or_1_out, WRITE_ADDR[0], WRITE_ADDR[1], WRITE_ADDR[2], WRITE_ADDR[3], WRITE_ADDR[4]);
  Multiplexer #(.select(2)) multiplexer_1 (
    .in0(WRITE), .in1(1'b0), .in2(WRITE), .in3(WRITE), .out(multiplexer_1_out[0]), .sel({CLOCK, LOAD}));
  and and_1 (and_1_out[0], CLOCK, WRITE);
  and and_2 (and_2_out, or_1_out, WRITE);
  Multiplexer #(.select(2), .width(5)) multiplexer_2 (
    .in0(R1A), .in1(WRITE_ADDR), .in2({5{1'b0}}), .in3({5{1'b0}}), .out(multiplexer_2_out),
    .sel({CLR_x0, multiplexer_1_out[0]}));
  Multiplexer #(.select(2), .width(5)) multiplexer_3 (
    .in0(R2A), .in1(WRITE_ADDR), .in2({5{1'b0}}), .in3({5{1'b0}}), .out(multiplexer_3_out),
    .sel({CLR_x0, multiplexer_1_out[0]}));
  Multiplexer #(.select(2)) multiplexer_4 (
    .in0(LOAD), .in1(1'b0), .in2(1'b0), .in3(1'b0), .out(multiplexer_4_out), .sel({CLR_x0, and_1_out[0]}));
  not not_1 (not_1_out, CLOCK);
  not not_2 (not_2_out, not_3_out);
  not not_3 (not_3_out, not_10_out);
  not not_4 (not_4_out, not_2_out);
  not not_5 (not_5_out, not_6_out);
  not not_6 (not_6_out, not_14_out);
  not not_7 (not_7_out, not_5_out);
  or or_2 (or_2_out, and_2_out, CLR_x0);
  // Probe on multiplexer_2_out
  // Probe on multiplexer_3_out
  not not_8 (not_8_out, not_1_out);
  not not_9 (not_9_out, not_8_out);
  not not_10 (not_10_out, not_11_out);
  not not_11 (not_11_out, not_18_out);
  not not_12 (not_12_out, not_4_out);
  not not_13 (not_13_out, not_12_out);
  not not_14 (not_14_out, not_15_out);
  not not_15 (not_15_out, not_19_out);
  not not_16 (not_16_out, not_7_out);
  not not_17 (not_17_out, not_16_out);
  and and_3 (and_3_out, CLOCK, or_2_out);
  not not_18 (not_18_out, not_9_out);
  not not_19 (not_19_out, not_13_out);
  not not_20 (not_20_out, not_17_out);
  RAM #(.addrWidth(5), .databus("bidir"), .enables("line")) ram_1 (
    .addr(multiplexer_2_out), .data(R1O[7:0]));  // open: we, oe, clk
  RAM #(.addrWidth(5), .databus("bidir"), .enables("line")) ram_2 (
    .addr(multiplexer_2_out), .data(R1O[15:8]));  // open: we, oe, clk
  RAM #(.addrWidth(5), .databus("bidir"), .enables("line")) ram_3 (
    .addr(multiplexer_2_out), .data(R1O[23:16]));  // open: we, oe, clk
  RAM #(.addrWidth(5), .databus("bidir"), .enables("line")) ram_4 (
    .addr(multiplexer_2_out), .data(R1O[31:24]));  // open: we, oe, clk
  Multiplexer #(.width(32)) multiplexer_5 (.in0(WRITE_DATA), .in1({32{1'b0}}), .out(multiplexer_5_out), .sel(CLR_x0));
  or or_3 (or_3_out, WRITE, CLR_x0);
  assign controlled_buffer_1_out = and_4_out ? multiplexer_5_out : 32'bz;  // Controlled_Buffer controlled_buffer_1
  // Probe on multiplexer_5_out
  and and_4 (and_4_out, CLOCK, or_3_out);
  assign R1O[31:24] = controlled_buffer_1_out[31:24];  // Buffer buffer_1, 8 bits wide
  assign R1O[23:16] = controlled_buffer_1_out[23:16];  // Buffer buffer_2, 8 bits wide
  not not_21 (not_21_out, CLOCK);
  not not_22 (not_22_out, not_23_out);
  not not_23 (not_23_out, not_31_out);
  not not_24 (not_24_out, not_22_out);
  not not_25 (not_25_out, not_26_out);
  not not_26 (not_26_out, not_36_out);
  not not_27 (not_27_out, not_25_out);
  assign R2O[7:0] = controlled_buffer_1_out[7:0];  // Buffer buffer_3, 8 bits wide
  assign R2O[15:8] = controlled_buffer_1_out[15:8];  // Buffer buffer_4, 8 bits wide
  assign R2O[23:16] = controlled_buffer_1_out[23:16];  // Buffer buffer_5, 8 bits wide
  assign R2O[31:24] = controlled_buffer_1_out[31:24];  // Buffer buffer_6, 8 bits wide
  assign R1O[15:8] = controlled_buffer_1_out[15:8];  // Buffer buffer_7, 8 bits wide
  assign R1O[7:0] = controlled_buffer_1_out[7:0];  // Buffer buffer_8, 8 bits wide
  not not_28 (not_28_out, not_21_out);
  not not_29 (not_29_out, not_28_out);
  not not_30 (not_30_out, not_29_out);
  not not_31 (not_31_out, not_32_out);
  not not_32 (not_32_out, not_30_out);
  not not_33 (not_33_out, not_24_out);
  not not_34 (not_34_out, not_33_out);
  not not_35 (not_35_out, not_34_out);
  not not_36 (not_36_out, not_37_out);
  not not_37 (not_37_out, not_35_out);
  not not_38 (not_38_out, not_27_out);
  not not_39 (not_39_out, not_38_out);
  not not_40 (not_40_out, not_39_out);
  RAM #(.addrWidth(5), .databus("bidir"), .enables("line")) ram_5 (
    .addr(multiplexer_3_out), .data(R2O[7:0]));  // open: we, oe, clk
  RAM #(.addrWidth(5), .databus("bidir"), .enables("line")) ram_6 (
    .addr(multiplexer_3_out), .data(R2O[15:8]));  // open: we, oe, clk
  RAM #(.addrWidth(5), .databus("bidir"), .enables("line")) ram_7 (
    .addr(multiplexer_3_out), .data(R2O[23:16]));  // open: we, oe, clk
  RAM #(.addrWidth(5), .databus("bidir"), .enables("line")) ram_8 (
    .addr(multiplexer_3_out), .data(R2O[31:24]));  // open: we, oe, clk

  // Other names for the same wires on the sheet: init = CLR_x0; read_reg_1_adr[4:0] = R1A; read_reg_2_adr[4:0] = R2A;
  //   reg_1_out[31:0] = R1O; reg_2_out[31:0] = R2O

  // Notes on the sheet:
  //   Long delay so that load and write work at once
endmodule

module alu (
  input  [2:0] INSTR,
  input  [31:0] X,
  input  [31:0] Y,
  output [31:0] O
);

  Decoder #(.select(3)) decoder_1 (.sel(INSTR));  // open: out0, out1, out2, out3, out4, out5, out6, out7, en
  quad_AND quad_and_1 (.X(X[3:0]), .Y(Y[3:0]), .out_4(O[3:0]));  // open: OE
  quad_AND quad_and_2 (.X(X[7:4]), .Y(Y[7:4]), .out_4(O[7:4]));  // open: OE
  quad_AND quad_and_3 (.X(X[11:8]), .Y(Y[11:8]), .out_4(O[11:8]));  // open: OE
  quad_AND quad_and_4 (.X(X[15:12]), .Y(Y[15:12]), .out_4(O[15:12]));  // open: OE
  quad_AND quad_and_5 (.X(X[19:16]), .Y(Y[19:16]), .out_4(O[19:16]));  // open: OE
  quad_AND quad_and_6 (.X(X[23:20]), .Y(Y[23:20]), .out_4(O[23:20]));  // open: OE
  quad_AND quad_and_7 (.X(X[27:24]), .Y(Y[27:24]), .out_4(O[27:24]));  // open: OE
  quad_AND quad_and_8 (.X(X[31:28]), .Y(Y[31:28]), .out_4(O[31:28]));  // open: OE
endmodule

module quad_AND (
  input  OE,
  input  [3:0] X,
  input  [3:0] Y,
  output [3:0] out_4
);

  wire and_1_out, and_2_out, and_3_out, and_4_out;

  and and_1 (and_1_out, X[0], Y[0]);
  and and_2 (and_2_out, X[1], Y[1]);
  and and_3 (and_3_out, X[2], Y[2]);
  and and_4 (and_4_out, X[3], Y[3]);
  assign out_4[0] = OE ? and_1_out : 1'bz;  // Controlled_Buffer controlled_buffer_1
  assign out_4[1] = OE ? and_2_out : 1'bz;  // Controlled_Buffer controlled_buffer_2
  assign out_4[2] = OE ? and_3_out : 1'bz;  // Controlled_Buffer controlled_buffer_3
  assign out_4[3] = OE ? and_4_out : 1'bz;  // Controlled_Buffer controlled_buffer_4
endmodule

module quad_OR (
  input  OE,
  input  [3:0] X,
  input  [3:0] Y,
  output [3:0] out_4
);

  wire or_1_out, or_2_out, or_3_out, or_4_out;

  or or_1 (or_1_out, X[0], Y[0]);
  or or_2 (or_2_out, X[1], Y[1]);
  or or_3 (or_3_out, X[2], Y[2]);
  or or_4 (or_4_out, X[3], Y[3]);
  assign out_4[0] = OE ? or_1_out : 1'bz;  // Controlled_Buffer controlled_buffer_1
  assign out_4[1] = OE ? or_2_out : 1'bz;  // Controlled_Buffer controlled_buffer_2
  assign out_4[2] = OE ? or_3_out : 1'bz;  // Controlled_Buffer controlled_buffer_3
  assign out_4[3] = OE ? or_4_out : 1'bz;  // Controlled_Buffer controlled_buffer_4
endmodule

module quad_XOR (
  input  OE,
  input  [3:0] X,
  input  [3:0] Y,
  output [3:0] out_4
);

  wire xor_1_out, xor_2_out, xor_3_out, xor_4_out;

  xor xor_1 (xor_1_out, X[0], Y[0]);
  xor xor_2 (xor_2_out, X[1], Y[1]);
  xor xor_3 (xor_3_out, X[2], Y[2]);
  xor xor_4 (xor_4_out, X[3], Y[3]);
  assign out_4[0] = OE ? xor_1_out : 1'bz;  // Controlled_Buffer controlled_buffer_1
  assign out_4[1] = OE ? xor_2_out : 1'bz;  // Controlled_Buffer controlled_buffer_2
  assign out_4[2] = OE ? xor_3_out : 1'bz;  // Controlled_Buffer controlled_buffer_3
  assign out_4[3] = OE ? xor_4_out : 1'bz;  // Controlled_Buffer controlled_buffer_4
endmodule
